// Digital circuit 4bit_full_adder.dig as structural Verilog
module _4bit_full_adder (
  input  [3:0] A,
  input  [3:0] B,
  input  Control,
  output [3:0] Sum,
  output Cout
);

  wire _1bit_full_adder_1_p5, _1bit_full_adder_2_p5, _1bit_full_adder_3_p5;

  // _1bit_full_adder _1bit_full_adder_1: pin names not known; wires that end beside it: A[0], B[0], Control, Sum[0], _1bit_full_adder_1_p5
  // _1bit_full_adder _1bit_full_adder_2: pin names not known; wires that end beside it: A[1], B[1], _1bit_full_adder_1_p5, Sum[1], _1bit_full_adder_2_p5
  // _1bit_full_adder _1bit_full_adder_3: pin names not known; wires that end beside it: A[2], B[2], _1bit_full_adder_2_p5, Sum[2], _1bit_full_adder_3_p5
  // _1bit_full_adder _1bit_full_adder_4: pin names not known; wires that end beside it: A[3], B[3], _1bit_full_adder_3_p5, Sum[3], Cout
endmodule
