// Digital circuit 4bit_subtractor.dig as structural Verilog
module _4bit_subtractor (
  input  [3:0] A,
  input  [3:0] B,
  input  Control,
  output [3:0] Result,
  output Cout
);

  wire [3:0] xor_1_out;

  xor xor_1 (xor_1_out[0], Control, B[0]);
  xor xor_2 (xor_1_out[1], Control, B[1]);
  xor xor_3 (xor_1_out[2], Control, B[2]);
  xor xor_4 (xor_1_out[3], Control, B[3]);
  _4bit_full_adder _4bit_full_adder_1 (.A(A), .B(xor_1_out), .Control(Control), .Sum(Result), .Cout(Cout));
endmodule
